# Fritzing sketch esquematicos (saved by Fritzing 0.9.3b)
breadboards: 1

parts:
  Componente1 = Arduino Uno (Rev3)
  Q1 = PHOTOTRANSISTOR REFLECTIVE OBJECT SENSOR [package=qrb1114-side]
  Componente2 = Bluetooth HC-05 Macho
  R1 = Resistor [tolerance=±5% resistance=220k package="0805 [SMD]"]
  R2 = Resistor [tolerance=±5% resistance=220 package="0805 [SMD]"]

nets:
  N1: Componente1.A1, Q1.E, R1.Pin_0
  N2: Componente1.D10_PWM/SS, Componente2.TXD
  N3: Componente1.D11_PWM/MOSI, Componente2.RXD
  GND: Componente1.GND, Q1.C, Q1.K, Componente2.GND
  5V: Componente1.5V, Componente2.VCC, R1.Pin_1, R2.Pin_1
  N4: Q1.A, R2.Pin_0

// code stored in the sketch: fritzingopticbt.ino
#include <SoftwareSerial.h>
SoftwareSerial Bluetooth(10, 11); //RX and TX HC05 sensor
int valor;


void setup() {
  // put your setup code here, to run once:
Bluetooth.begin(9600);
Serial.begin(9600);
}


void loop() {
  // put your main code here, to run repeatedly:
  valor = analogRead(1);
 
  if(valor < 750){
    Bluetooth.println("a");
    //Serial.println(valor);
    delay(2800);
      }
      
}
